# Fritzing sketch glide-lock-attiny (saved by Fritzing 0.9.6b)
breadboards: 1

parts:
  2S_LIPO_8_4v = LIPO-2000mAh [package=lipo-2000]
  Hall_Sensor = HALL-EFFECT [package=sc70]
  Speed_Controller = BL Esc [chip_label=BL-ESC package="DIP (Dual Inline) [THT]"]
  Brushless_Motor = DC Motor
  Digital_->_P0_|_Analog_->_P4 = SO08 [chip_label=ATTiny85 package=SO]
  Receiver = IC, SIP package, 8 pins [chip_label=RX]

nets:
  N1: 2S_LIPO_8_4v.+, Speed_Controller.VIN
  N2: 2S_LIPO_8_4v.-, Speed_Controller.GND
  N3: Hall_Sensor.GND, Digital_->_P0_|_Analog_->_P4.1, Receiver.pin1
  N4: Hall_Sensor.VCC, Speed_Controller.VOUT-5v, Digital_->_P0_|_Analog_->_P4.2, Receiver.pin2
  N5: Hall_Sensor.OUT, Digital_->_P0_|_Analog_->_P4.3, Digital_->_P0_|_Analog_->_P4.7
  N6: Speed_Controller.SIGNAL, Digital_->_P0_|_Analog_->_P4.6
  N7: Speed_Controller.M3, Speed_Controller.M2, Brushless_Motor.pin_2
  N8: Speed_Controller.M1, Brushless_Motor.pin_1
  N9: Digital_->_P0_|_Analog_->_P4.5, Receiver.pin5

custom parts:
  BL Esc: Generic RC speed controller for 3-phase brushless motor.
