# Fritzing sketch glide-lock-nano (saved by Fritzing 0.9.3b)
breadboards: 1

parts:
  2S_LIPO_8_4v = LIPO-2000mAh [package=lipo-2000]
  Part1 = Arduino Nano (Rev3.0) (ICSP)
  Analog_Hall_Sensor = HALL-EFFECT [package=sc70]
  Receiver = reciever [chip_label=RX]
  Speed_Controller = BL Esc [chip_label=BL-ESC package="DIP (Dual Inline) [THT]"]
  Brushless_Motor = DC Motor

nets:
  VIN: 2S_LIPO_8_4v.+, Part1.VIN, Speed_Controller.VIN
  GND: 2S_LIPO_8_4v.-, Part1.GND, Analog_Hall_Sensor.GND, Receiver.connector1, Speed_Controller.GND
  N1: Part1.D2, Speed_Controller.SIGNAL
  N2: Part1.D3, Receiver.connector4
  5V: Part1.5V, Analog_Hall_Sensor.VCC, Receiver.connector0, Speed_Controller.VOUT-5v
  N3: Part1.A0, Analog_Hall_Sensor.OUT
  N4: Speed_Controller.M3, Speed_Controller.M2, Brushless_Motor.pin_2
  N5: Speed_Controller.M1, Brushless_Motor.pin_1

custom parts:
  BL Esc: Generic RC speed controller for 3-phase brushless motor.
